// Logisim project LC3-2200a.circ as structural Verilog: 5 circuits, main circuit Datapath
module Datapath (
  input  in_1,
  input  in_2,
  input  in_3,
  input  in_4,
  input  in_5,
  input  in_6,
  input  in_7,
  input  in_8,
  input  [1:0] in_9,
  input  in_10,
  input  in_11,
  input  in_12,
  input  in_13,
  input  in_14,
  input  [1:0] in_15,
  input  in_16,
  output [3:0] out_17,
  output out_18
);

  wire A, D, n_out, or_1_out, p_out, z_out;
  wire [2:0] CC, comparator_1_gt, register_1_q;
  wire [3:0] Regno, Rx, Rz;
  wire [3:3] Ry;
  wire [17:4] IR_q;
  wire [31:0] A_q, alu_1_out, B_q, bit_extender_1_out, controlled_buffer_1_out, MAR_q, PC_q, ram_1_data,
       registers_1_out_5;

  Register #(.width(32)) PC (.D(controlled_buffer_1_out), .en(in_2), .Q(PC_q), .clk(in_12));  // open: clr
  assign controlled_buffer_1_out = in_1 ? PC_q : 32'bz;  // Controlled_Buffer controlled_buffer_1
  Comparator #(.width(32), .mode("unsigned")) comparator_1 (
    .a(controlled_buffer_1_out), .b({32{1'b0}}), .gt(comparator_1_gt[0]), .eq(comparator_1_gt[1]),
    .lt(comparator_1_gt[2]));
  Register #(.width(3)) register_1 (.D(comparator_1_gt), .en(in_16), .Q(register_1_q), .clk(in_12));  // open: clr
  Register #(.width(32)) u_A (.D(controlled_buffer_1_out), .en(in_5), .Q(A_q), .clk(in_12));  // open: clr
  ALU alu_1 (.A(A_q), .B(B_q), .Out(alu_1_out), .Func(in_9), .A_2(A), .D(D));
  assign controlled_buffer_1_out = in_4 ? alu_1_out : 32'bz;  // Controlled_Buffer controlled_buffer_2
  Register #(.width(32)) B (.D(controlled_buffer_1_out), .en(in_8), .Q(B_q), .clk(in_12));  // open: clr
  and p (p_out, register_1_q[0], CC[0]);
  and z (z_out, register_1_q[1], CC[1]);
  and n (n_out, register_1_q[2], CC[2]);
  Registers registers_1 (
    .in_1(Regno), .in_2(in_6), .in_3(in_12), .in_4(controlled_buffer_1_out), .out_5(registers_1_out_5));
  or or_1 (or_1_out, p_out, z_out);
  or or_2 (out_18, or_1_out, n_out);
  Multiplexer #(.select(2), .width(4), .disabled(0), .enable("false")) multiplexer_1 (
    .in0(Rx), .in1({Ry[3], CC}), .in2(Rz), .out(Regno), .sel(in_15));  // open: in3
  Register #(.width(32)) MAR (.D(controlled_buffer_1_out), .en(in_11), .Q(MAR_q), .clk(in_12));  // open: clr
  assign controlled_buffer_1_out = in_7 ? registers_1_out_5 : 32'bz;  // Controlled_Buffer controlled_buffer_3
  Register #(.width(32)) IR (
    .D(controlled_buffer_1_out), .en(in_14), .Q({out_17, Rx, Ry[3], CC, A, D, IR_q, Rz}), .clk(in_12));  // open: clr
  RAM #(.addrWidth(24), .dataWidth(32), .bus("separate")) ram_1 (
    .addr(MAR_q[31:8]), .din(controlled_buffer_1_out), .data(ram_1_data), .str(in_3), .clk(in_12));  // open: sel, ld, clr
  assign controlled_buffer_1_out = in_10 ? ram_1_data : 32'bz;  // Controlled_Buffer controlled_buffer_4
  assign bit_extender_1_out = {{12{A}}, {A, D, IR_q, Rz}};  // Bit_Extender bit_extender_1
  assign controlled_buffer_1_out = in_13 ? bit_extender_1_out : 32'bz;  // Controlled_Buffer controlled_buffer_5

  // Other names for the same wires on the sheet: Ry[2:0] = CC; OP[3:0] = out_17; CCMatch = out_18; Clk = in_12;
  //   DrALU = in_4; DrMem = in_10; DrOff = in_13; DrPC = in_1; DrReg = in_7; Func[1:0] = in_9; LdA = in_5; LdB = in_8;
  //   LdCC = in_16; LdIR = in_14; LdMAR = in_11; LdPC = in_2; RegSel[1:0] = in_15; WrMem = in_3; WrReg = in_6

  // Notes on the sheet:
  //   Zhijian Li
  //   903078127
  //   Rx: 00
  //   Ry: 01
  //   Rz: 10
endmodule

module ALU (
  input  [31:0] A,
  input  [31:0] B,
  input  A_2,
  input  D,
  input  [1:0] Func,
  output [31:0] Out
);

  wire [31:0] adder_1_out, adder_2_out, multiplexer_1_out, nand_1_out, shifter_1_out, shifter_2_out,
       shifter_3_out;

  Shifter #(.width(32)) shifter_1 (.in(A), .\dist (B[4:0]), .out(shifter_1_out));
  Shifter #(.width(32), .shift("lr")) shifter_2 (.in(A), .\dist (B[4:0]), .out(shifter_2_out));
  Shifter #(.width(32), .shift("ar")) shifter_3 (.in(A), .\dist (B[4:0]), .out(shifter_3_out));
  Adder #(.width(32)) adder_1 (.a(A), .b(B), .out(adder_1_out));  // open: cin, cout
  assign nand_1_out = ~(A & B);  // NAND_Gate nand_1, 32 bits wide
  Adder #(.width(32)) adder_2 (.a(A), .b(32'h1), .out(adder_2_out));  // open: cin, cout
  Multiplexer #(.select(2), .width(32), .disabled(0), .enable("false")) multiplexer_1 (
    .in0(shifter_1_out), .in1(shifter_2_out), .in2(shifter_1_out), .in3(shifter_3_out),
    .out(multiplexer_1_out), .sel({A_2, D}));
  Multiplexer #(.select(2), .width(32), .disabled(0), .enable("false")) multiplexer_2 (
    .in0(adder_1_out), .in1(nand_1_out), .in2(adder_2_out), .in3(multiplexer_1_out), .out(Out), .sel(Func));
endmodule

module Micro_sequencer (
  input  in_1,
  input  [3:0] in_2,
  input  in_3,
  output out_4,
  output out_5,
  output out_6,
  output out_7,
  output out_8,
  output out_9,
  output out_10,
  output out_11,
  output out_12,
  output out_13,
  output out_14,
  output [1:0] out_15,
  output out_16,
  output [1:0] out_17,
  output out_18
);

  wire [5:0] multiplexer_1_out, rom_2_data, rom_3_data, State;
  wire [24:0] rom_1_data;

  ROM #(.addrWidth(6), .dataWidth(25)) rom_1 (
    .addr(State),
    .data({rom_1_data[24:23], out_15, out_17, out_16, out_18, out_14, out_9, out_7, out_11, out_13, out_5, out_12, out_4, out_6, out_10, out_8, rom_1_data[5:0]}));  // open: sel
  ROM #(.addrWidth(4), .dataWidth(6)) rom_2 (.addr(in_2), .data(rom_2_data));  // open: sel
  ROM #(.addrWidth(2), .dataWidth(6)) rom_3 (.addr({1'b0, in_3}), .data(rom_3_data));  // open: sel
  Multiplexer #(.select(2), .width(6), .disabled(0), .enable("false")) multiplexer_1 (
    .in0(rom_1_data[5:0]), .in1(rom_2_data), .in2(rom_3_data), .out(multiplexer_1_out),
    .sel(rom_1_data[24:23]));  // open: in3
  Register #(.width(6)) Next_State (.D(multiplexer_1_out), .Q(State), .clk(in_1));  // open: en, clr

  // Other names for the same wires on the sheet: DrReg = out_8; DrMem = out_10; DrALU = out_6; DrPC = out_4;
  //   DrOff = out_12; LdPC = out_5; LdIR = out_13; LdMAR = out_11; LdA = out_7; LdB = out_9; LdCC = out_14;
  //   WrReg = out_18; WrMem = out_16; RegSel[1:0] = out_17; Func[1:0] = out_15; CCMatch = in_3; Clk = in_1;
  //   OP[3:0] = in_2

  // Notes on the sheet:
  //   contents of rom_1 (hex, n*v repeats v):
  //   6201 1082 400903 800000 84045 108046 30100 84048 8409 30100 8404b 10804c 230100 404e 804f 1210100
  //   4211 8412 900 20214 80840 84056 8417 2118 30080 421a 841b 30100 10405d 841e 211f 40040 84061 8422
  //   630100 23
  //   contents of rom_2 (hex, n*v repeats v):
  //   4 7 a d 13 15 19 1c 20 6*0 23
  //   contents of rom_3 (hex, n*v repeats v):
  //   0 10
endmodule

module Registers (
  input  [3:0] in_1,
  input  in_2,
  input  in_3,
  input  [31:0] in_4,
  output [31:0] out_5
);

  wire decoder_1_out1, decoder_1_out2, decoder_1_out3, decoder_1_out4, decoder_1_out5, decoder_1_out6,
       decoder_1_out7, decoder_1_out8, decoder_1_out9, decoder_1_out10, decoder_1_out11, decoder_1_out12,
       decoder_1_out13, decoder_1_out14, decoder_1_out15;
  wire [3:0] bit_extender_1_out, RegnoWr;
  wire [31:0] a0_q, a1_q, a2_q, at_q, fp_q, k0_q, ra_q, s0_q, s1_q, s2_q, sp_q, t0_q, t1_q, t2_q, v0_q;

  Decoder #(.select(4), .enable("false")) decoder_1 (
    .out1(decoder_1_out1), .out2(decoder_1_out2), .out3(decoder_1_out3), .out4(decoder_1_out4),
    .out5(decoder_1_out5), .out6(decoder_1_out6), .out7(decoder_1_out7), .out8(decoder_1_out8),
    .out9(decoder_1_out9), .out10(decoder_1_out10), .out11(decoder_1_out11), .out12(decoder_1_out12),
    .out13(decoder_1_out13), .out14(decoder_1_out14), .out15(decoder_1_out15), .sel(RegnoWr));  // open: out0
  Register #(.width(32)) at (.D(in_4), .en(decoder_1_out1), .Q(at_q), .clk(in_3));  // open: clr
  Register #(.width(32)) v0 (.D(in_4), .en(decoder_1_out2), .Q(v0_q), .clk(in_3));  // open: clr
  Register #(.width(32)) a0 (.D(in_4), .en(decoder_1_out3), .Q(a0_q), .clk(in_3));  // open: clr
  Register #(.width(32)) a1 (.D(in_4), .en(decoder_1_out4), .Q(a1_q), .clk(in_3));  // open: clr
  Register #(.width(32)) a2 (.D(in_4), .en(decoder_1_out5), .Q(a2_q), .clk(in_3));  // open: clr
  Register #(.width(32)) t0 (.D(in_4), .en(decoder_1_out6), .Q(t0_q), .clk(in_3));  // open: clr
  Register #(.width(32)) t1 (.D(in_4), .en(decoder_1_out7), .Q(t1_q), .clk(in_3));  // open: clr
  Register #(.width(32)) t2 (.D(in_4), .en(decoder_1_out8), .Q(t2_q), .clk(in_3));  // open: clr
  Register #(.width(32)) s0 (.D(in_4), .en(decoder_1_out9), .Q(s0_q), .clk(in_3));  // open: clr
  Register #(.width(32)) s1 (.D(in_4), .en(decoder_1_out10), .Q(s1_q), .clk(in_3));  // open: clr
  Register #(.width(32)) s2 (.D(in_4), .en(decoder_1_out11), .Q(s2_q), .clk(in_3));  // open: clr
  Register #(.width(32)) k0 (.D(in_4), .en(decoder_1_out12), .Q(k0_q), .clk(in_3));  // open: clr
  Register #(.width(32)) sp (.D(in_4), .en(decoder_1_out13), .Q(sp_q), .clk(in_3));  // open: clr
  Register #(.width(32)) fp (.D(in_4), .en(decoder_1_out14), .Q(fp_q), .clk(in_3));  // open: clr
  Register #(.width(32)) ra (.D(in_4), .en(decoder_1_out15), .Q(ra_q), .clk(in_3));  // open: clr
  Multiplexer #(.select(4), .width(32), .disabled(0), .enable("false")) multiplexer_1 (
    .in0({32{1'b0}}), .in1(at_q), .in2(v0_q), .in3(a0_q), .in4(a1_q), .in5(a2_q), .in6(t0_q), .in7(t1_q),
    .in8(t2_q), .in9(s0_q), .in10(s1_q), .in11(s2_q), .in12(k0_q), .in13(sp_q), .in14(fp_q), .in15(ra_q),
    .out(out_5), .sel(in_1));
  assign bit_extender_1_out = {{3{in_2}}, in_2};  // Bit_Extender bit_extender_1
  assign RegnoWr = bit_extender_1_out & in_1;  // AND_Gate and_1, 4 bits wide

  // Other names for the same wires on the sheet: Clk = in_3; Din[31:0] = in_4; Dout[31:0] = out_5; Regno[3:0] = in_1;
  //   WrReG = in_2
endmodule

module main (
);

  wire clock_1_out, datapath_1_out_18, micro_sequencer_1_out_4, micro_sequencer_1_out_5,
       micro_sequencer_1_out_6, micro_sequencer_1_out_7, micro_sequencer_1_out_8, micro_sequencer_1_out_9,
       micro_sequencer_1_out_10, micro_sequencer_1_out_11, micro_sequencer_1_out_12,
       micro_sequencer_1_out_13, micro_sequencer_1_out_14, micro_sequencer_1_out_16, micro_sequencer_1_out_18;
  wire [1:0] micro_sequencer_1_out_15, micro_sequencer_1_out_17;
  wire [3:0] datapath_1_out_17;

  Datapath datapath_1 (
    .in_1(micro_sequencer_1_out_4), .in_2(micro_sequencer_1_out_5), .in_3(micro_sequencer_1_out_16),
    .in_4(micro_sequencer_1_out_6), .in_5(micro_sequencer_1_out_7), .in_6(micro_sequencer_1_out_18),
    .in_7(micro_sequencer_1_out_8), .in_8(micro_sequencer_1_out_9), .in_9(micro_sequencer_1_out_15),
    .in_10(micro_sequencer_1_out_10), .in_11(micro_sequencer_1_out_11), .in_13(micro_sequencer_1_out_12),
    .in_14(micro_sequencer_1_out_13), .in_15(micro_sequencer_1_out_17), .in_16(micro_sequencer_1_out_14),
    .out_17(datapath_1_out_17), .out_18(datapath_1_out_18), .in_12(clock_1_out));
  Clock clock_1 (.out(clock_1_out));
  Micro_sequencer micro_sequencer_1 (
    .in_1(clock_1_out), .in_2(datapath_1_out_17), .in_3(datapath_1_out_18), .out_4(micro_sequencer_1_out_4),
    .out_5(micro_sequencer_1_out_5), .out_6(micro_sequencer_1_out_6), .out_7(micro_sequencer_1_out_7),
    .out_8(micro_sequencer_1_out_8), .out_9(micro_sequencer_1_out_9), .out_10(micro_sequencer_1_out_10),
    .out_11(micro_sequencer_1_out_11), .out_12(micro_sequencer_1_out_12), .out_13(micro_sequencer_1_out_13),
    .out_14(micro_sequencer_1_out_14), .out_15(micro_sequencer_1_out_15), .out_18(micro_sequencer_1_out_18),
    .out_17(micro_sequencer_1_out_17), .out_16(micro_sequencer_1_out_16));
endmodule
