// Logisim project LC3-2200a.circ as structural Verilog: 3 circuits, main circuit Datapath
module Datapath (
  input  in_1,
  input  in_2,
  input  in_3,
  input  in_4,
  input  in_5,
  input  in_6,
  input  in_7,
  input  in_8,
  input  [1:0] in_9,
  input  in_10,
  input  in_11,
  input  in_12,
  input  in_13,
  input  [1:0] in_14,
  input  in_15,
  input  in_16,
  output [3:0] out_17,
  output out_18
);

  wire A, Clk, D, n_out, or_1_out, or_2_out, p_out, z_out;
  wire [2:0] CC, comparator_1_gt, register_1_q;
  wire [3:0] Regno, Rx, Rz;
  wire [3:3] Ry;
  wire [17:4] IR_q;
  wire [31:0] A_q, alu_1_out, B_q, bit_extender_1_out, controlled_buffer_1_out, MAR_q, PC_q, ram_1_data,
       ram_2_data;

  Register #(.width(32)) PC (.D(controlled_buffer_1_out), .en(in_2), .Q(PC_q), .clk(Clk));  // open: clr
  assign controlled_buffer_1_out = in_1 ? PC_q : 32'bz;  // Controlled_Buffer controlled_buffer_1
  Comparator #(.width(32), .mode("unsigned")) comparator_1 (
    .a(controlled_buffer_1_out), .b({32{1'b0}}), .gt(comparator_1_gt[0]), .eq(comparator_1_gt[1]),
    .lt(comparator_1_gt[2]));
  Register #(.width(3)) register_1 (.D(comparator_1_gt), .en(in_15), .Q(register_1_q), .clk(Clk));  // open: clr
  Register #(.width(32)) u_A (.D(controlled_buffer_1_out), .en(in_5), .Q(A_q), .clk(Clk));  // open: clr
  ALU alu_1 (.A(A_q), .B(B_q), .Out(alu_1_out), .Func(in_9), .A_2(A), .D(D));
  assign controlled_buffer_1_out = in_4 ? alu_1_out : 32'bz;  // Controlled_Buffer controlled_buffer_2
  Clock clock_1 (.out(Clk));
  Register #(.width(32)) B (.D(controlled_buffer_1_out), .en(in_8), .Q(B_q), .clk(Clk));  // open: clr
  and p (p_out, register_1_q[0], CC[0]);
  and z (z_out, register_1_q[1], CC[1]);
  and n (n_out, register_1_q[2], CC[2]);
  or or_1 (or_1_out, p_out, z_out);
  or or_2 (or_2_out, or_1_out, n_out);
  assign out_18 = in_16 ? or_2_out : 1'bz;  // Controlled_Buffer controlled_buffer_3
  Multiplexer #(.select(2), .width(4), .disabled(0), .enable("false")) multiplexer_1 (
    .in0(Rx), .in1({Ry[3], CC}), .in2(Rz), .out(Regno), .sel(in_14));  // open: in3
  Register #(.width(32)) MAR (.D(controlled_buffer_1_out), .en(in_11), .Q(MAR_q), .clk(Clk));  // open: clr
  RAM #(.addrWidth(4), .dataWidth(32), .bus("separate")) ram_1 (
    .addr(Regno), .din(controlled_buffer_1_out), .data(ram_1_data), .str(in_6), .clk(Clk));  // open: sel, ld, clr
  assign controlled_buffer_1_out = in_7 ? ram_1_data : 32'bz;  // Controlled_Buffer controlled_buffer_4
  Register #(.width(32)) IR (
    .D(controlled_buffer_1_out), .en(in_13), .Q({out_17, Rx, Ry[3], CC, A, D, IR_q, Rz}), .clk(Clk));  // open: clr
  RAM #(.addrWidth(24), .dataWidth(32), .bus("separate")) ram_2 (
    .addr(MAR_q[31:8]), .din(controlled_buffer_1_out), .data(ram_2_data), .str(in_3), .clk(Clk));  // open: sel, ld, clr
  assign controlled_buffer_1_out = in_10 ? ram_2_data : 32'bz;  // Controlled_Buffer controlled_buffer_5
  Bit_Extender #(.in_width(20), .out_width(32), .\type ("input")) bit_extender_1 (
    .in({A, D, IR_q, Rz}), .out(bit_extender_1_out));  // open: extend
  assign controlled_buffer_1_out = in_12 ? bit_extender_1_out : 32'bz;  // Controlled_Buffer controlled_buffer_6

  // Other names for the same wires on the sheet: Ry[2:0] = CC; OP[3:0] = out_17; CCMatch = out_18; ChkCC = in_16;
  //   DrALU = in_4; DrMem = in_10; DrOff = in_12; DrPC = in_1; DrReg = in_7; Func[1:0] = in_9; LdA = in_5; LdB = in_8;
  //   LdCC = in_15; LdIR = in_13; LdMAR = in_11; LdPC = in_2; RegSel[1:0] = in_14; WrMem = in_3; WrReg = in_6

  // Notes on the sheet:
  //   Zhijian Li
  //   903078127
  //   Rx: 00
  //   Ry: 01
  //   Rz: 10
endmodule

module ALU (
  input  [31:0] A,
  input  [31:0] B,
  input  A_2,
  input  D,
  input  [1:0] Func,
  output [31:0] Out
);

  wire [31:0] adder_1_out, adder_2_out, multiplexer_1_out, nand_1_out, shifter_1_out, shifter_2_out,
       shifter_3_out;

  Shifter #(.width(32)) shifter_1 (.in(A), .\dist (B[4:0]), .out(shifter_1_out));
  Shifter #(.width(32), .shift("lr")) shifter_2 (.in(A), .\dist (B[4:0]), .out(shifter_2_out));
  Shifter #(.width(32), .shift("ar")) shifter_3 (.in(A), .\dist (B[4:0]), .out(shifter_3_out));
  Adder #(.width(32)) adder_1 (.a(A), .b(B), .out(adder_1_out));  // open: cin, cout
  assign nand_1_out = ~(A & B);  // NAND_Gate nand_1, 32 bits wide
  Adder #(.width(32)) adder_2 (.a(A), .b(32'h1), .out(adder_2_out));  // open: cin, cout
  Multiplexer #(.select(2), .width(32), .disabled(0), .enable("false")) multiplexer_1 (
    .in0(shifter_1_out), .in1(shifter_2_out), .in2(shifter_1_out), .in3(shifter_3_out),
    .out(multiplexer_1_out), .sel({A_2, D}));
  Multiplexer #(.select(2), .width(32), .disabled(0), .enable("false")) multiplexer_2 (
    .in0(adder_1_out), .in1(nand_1_out), .in2(adder_2_out), .in3(multiplexer_1_out), .out(Out), .sel(Func));
endmodule

module Micro_sequencer (
  input  in_1,
  input  [3:0] in_2,
  input  in_3,
  output out_4,
  output out_5,
  output out_6,
  output out_7,
  output out_8,
  output out_9,
  output out_10,
  output out_11,
  output out_12,
  output out_13,
  output out_14,
  output [1:0] out_15,
  output out_16,
  output [1:0] out_17,
  output out_18
);

  wire [5:0] multiplexer_1_out, rom_2_data, rom_3_data, State;
  wire [24:0] rom_1_data;

  ROM #(.addrWidth(6), .dataWidth(25)) rom_1 (
    .addr(State),
    .data({rom_1_data[24:23], out_17, out_15, out_18, out_16, out_14, out_13, out_11, out_9, out_7, out_5, out_12, out_10, out_8, out_6, out_4, rom_1_data[5:0]}));  // open: sel
  ROM #(.addrWidth(4), .dataWidth(6)) rom_2 (.addr(in_2), .data(rom_2_data));  // open: sel
  ROM #(.addrWidth(2), .dataWidth(6)) rom_3 (.addr({1'b0, in_3}), .data(rom_3_data));  // open: sel
  Multiplexer #(.select(2), .width(6), .disabled(0), .enable("false")) multiplexer_1 (
    .in0(rom_1_data[5:0]), .in1(rom_2_data), .in2(rom_3_data), .out(multiplexer_1_out),
    .sel(rom_1_data[24:23]));  // open: in3
  Register #(.width(6)) Next_State (.D(multiplexer_1_out), .Q(State), .clk(in_1));  // open: en, clr

  // Other names for the same wires on the sheet: DrReg = out_4; DrMem = out_6; DrALU = out_8; DrPC = out_10;
  //   DrOff = out_12; LdPC = out_5; LdIR = out_7; LdMAR = out_9; LdA = out_11; LdB = out_13; LdCC = out_14;
  //   WrReg = out_16; WrMem = out_18; RegSel[1:0] = out_15; Func[1:0] = out_17; CCMatch = in_3; Clk = in_1;
  //   OP[3:0] = in_2

  // Notes on the sheet:
  //   contents of rom_1 (hex, n*v repeats v):
  //   6201 1082 600903 800000 84045 108046 30100 84048 8409 30100 8404b 10804c 230100 404e 804f 1210100
  //   4211 8412 900 20214 80840 84056 8417 2118 30080 421a 841b 30100 10405d 841e 211f 40040 84061 8422
  //   630100 23
  //   contents of rom_2 (hex, n*v repeats v):
  //   4 7 a d 13 15 19 1c 20 23
  //   contents of rom_3 (hex, n*v repeats v):
  //   0 10
endmodule
