// Logisim project li_zhijian.circ as structural Verilog: 14 circuits, main circuit main
module main (
);

  wire CLK, ex_1_lw_out, ex_1_sw_out, ex_mem_buffer_1_lw_out, ex_mem_buffer_1_sw_out, id_1_br_cond,
       id_1_i_type, id_1_jalr, id_1_lw, id_1_shf_a, id_1_shf_d, id_1_sw, idrr_ex_buffer_1_lw_out,
       idrr_ex_buffer_1_shf_a_out, idrr_ex_buffer_1_shf_d_out, idrr_ex_buffer_1_sw_out, mem_1_sw_out,
       mem_wb_buffer_1_sw_out, Use_RZ, WB;
  wire [1:0] id_1_func, idrr_ex_buffer_1_func_out;
  wire [3:0] ex_mem_buffer_1_op_out, ex_mem_buffer_1_rx_out, EX_OP, EX_RX, id_1_op_out, id_1_rx_out,
       idrr_ex_buffer_1_op_out, idrr_ex_buffer_1_rx_out, if_idrr_buffer_1_op_out, MEM_OP, MEM_RX,
       mem_wb_buffer_1_op_out, mem_wb_buffer_1_rx_out, RX, RY, RZ, WB_RX;
  wire [19:0] if_idrr_buffer_1_imm_out;
  wire [31:0] A_IN, B_IN, B_OUT, ex_1_b_out, ex_mem_buffer_1_b_out, ex_mem_buffer_1_result_out, EX_Result,
       id_1_imm_out, id_1_result, idrr_ex_buffer_1_a_out, idrr_ex_buffer_1_b_out, idrr_ex_buffer_1_imm_out,
       if_1_ir_out, if_1_pc_out, if_idrr_buffer_1_pc_out, MEM_RESULT, mem_wb_buffer_1_result_out, RESULT;

  Clock CLOCK (.out(CLK));
  IF if_1 (
    .CLK(CLK), .JALR(id_1_jalr), .PC___Off(id_1_result), .JALR_PC(A_IN), .BR(id_1_br_cond),
    .PC_OUT(if_1_pc_out), .IR_OUT(if_1_ir_out));
  IF_IDRR_Buffer if_idrr_buffer_1 (
    .in_1(CLK), .PC_N(if_1_pc_out), .IR_IN(if_1_ir_out), .PC_OUT(if_idrr_buffer_1_pc_out),
    .OP_OUT(if_idrr_buffer_1_op_out), .RX_OUT(RX), .RY_OUT(RY), .RZ_OUT(RZ),
    .IMM_OUT(if_idrr_buffer_1_imm_out), .in_2(id_1_jalr));
  ID id_1 (
    .CLK(CLK), .IMM_IN(if_idrr_buffer_1_imm_out), .OP_IN(if_idrr_buffer_1_op_out),
    .PC_IN(if_idrr_buffer_1_pc_out), .RX_IN(RX), .RY_IN(RY), .RZ_IN(RZ), .I_Type(id_1_i_type),
    .SHF_A(id_1_shf_a), .SHF_D(id_1_shf_d), .BR_Cond(id_1_br_cond), .Func(id_1_func), .OP_OUT(id_1_op_out),
    .RESULT(id_1_result), .A_OUT(A_IN), .B_OUT(B_IN), .JALR(id_1_jalr), .IMM_OUT(id_1_imm_out),
    .RX_OUT(id_1_rx_out), .SW(id_1_sw), .LW(id_1_lw), .WB_RESULT(RESULT), .WB(WB), .WB_RX(WB_RX),
    .Use_RZ(Use_RZ), .NEW_A(A_IN), .NEW_B(B_OUT));
  Forwarder forwarder_1 (
    .E_RX(EX_RX), .M_RX(MEM_RX), .A(A_IN), .E_Result(EX_Result), .M_Result(MEM_RESULT), .B(B_IN), .RX(RX),
    .RY(RY), .RZ(RZ), .Use_RZ(Use_RZ), .A_OUT(A_IN), .B_OUT(B_OUT));
  IDRR_EX_Buffer idrr_ex_buffer_1 (
    .CLK(CLK), .IMM_IN(id_1_imm_out), .Result_IN(id_1_result), .A_IN(A_IN), .B_IN(B_OUT),
    .IMM_OUT(idrr_ex_buffer_1_imm_out), .A_OUT(idrr_ex_buffer_1_a_out), .B_OUT(idrr_ex_buffer_1_b_out),
    .OP_IN(id_1_op_out), .OP_OUT(idrr_ex_buffer_1_op_out), .RX_IN(id_1_rx_out),
    .RX_OUT(idrr_ex_buffer_1_rx_out), .Func_IN(id_1_func), .Func_OUT(idrr_ex_buffer_1_func_out),
    .SHF_A_IN(id_1_shf_a), .SHF_A_OUT(idrr_ex_buffer_1_shf_a_out), .SHF_D_IN(id_1_shf_d),
    .SHF_D_OUT(idrr_ex_buffer_1_shf_d_out), .SW_IN(id_1_sw), .SW_OUT(idrr_ex_buffer_1_sw_out),
    .LW_IN(id_1_lw), .LW_OUT(idrr_ex_buffer_1_lw_out));  // open: Result_OUT
  EX ex_1 (
    .Func(idrr_ex_buffer_1_func_out), .I_Type(id_1_i_type), .A_IN(idrr_ex_buffer_1_a_out),
    .B_IN(idrr_ex_buffer_1_b_out), .IMM_IN(idrr_ex_buffer_1_imm_out), .SHF_A(idrr_ex_buffer_1_shf_a_out),
    .SHF_D(idrr_ex_buffer_1_shf_d_out), .OP_IN(idrr_ex_buffer_1_op_out), .RX_IN(idrr_ex_buffer_1_rx_out),
    .OP_OUT(EX_OP), .RX_OUT(EX_RX), .B_OUT(ex_1_b_out), .RESULT(EX_Result), .SW_IN(idrr_ex_buffer_1_sw_out),
    .LW_IN(idrr_ex_buffer_1_lw_out), .SW_OUT(ex_1_sw_out), .LW_OUT(ex_1_lw_out));
  EX_MEM_Buffer ex_mem_buffer_1 (
    .SW_IN(ex_1_sw_out), .LW_IN(ex_1_lw_out), .RX_IN(EX_RX), .OP_IN(EX_OP), .B_IN(ex_1_b_out),
    .RESULT_IN(EX_Result), .SW_OUT(ex_mem_buffer_1_sw_out), .LW_OUT(ex_mem_buffer_1_lw_out),
    .RX_OUT(ex_mem_buffer_1_rx_out), .OP_OUT(ex_mem_buffer_1_op_out), .B_OUT(ex_mem_buffer_1_b_out),
    .RESULT_OUT(ex_mem_buffer_1_result_out), .in_1(CLK));
  MEM mem_1 (
    .CLK(CLK), .SW_IN(ex_mem_buffer_1_sw_out), .LW_IN(ex_mem_buffer_1_lw_out),
    .RX_IN(ex_mem_buffer_1_rx_out), .OP_IN(ex_mem_buffer_1_op_out), .B_IN(ex_mem_buffer_1_b_out),
    .RESULT_IN(ex_mem_buffer_1_result_out), .SW_OUT(mem_1_sw_out), .RX_OUT(MEM_RX), .OP_OUT(MEM_OP),
    .RESULT_OUT(MEM_RESULT));
  MEM_WB_Buffer mem_wb_buffer_1 (
    .CLK(CLK), .SW_IN(mem_1_sw_out), .RX_IN(MEM_RX), .OP_IN(MEM_OP), .RESULT_IN(MEM_RESULT),
    .SW_OUT(mem_wb_buffer_1_sw_out), .RX_OUT(mem_wb_buffer_1_rx_out), .OP_OUT(mem_wb_buffer_1_op_out),
    .RESULT_OUT(mem_wb_buffer_1_result_out));
  WB wb_1 (
    .SW_IN(mem_wb_buffer_1_sw_out), .RX_IN(mem_wb_buffer_1_rx_out), .OP_IN(mem_wb_buffer_1_op_out),
    .RESULT_IN(mem_wb_buffer_1_result_out), .out_5(WB), .RESULT_OUT(RESULT), .RX_OUT(WB_RX));

  // Other names for the same wires on the sheet: A_OUT[31:0] = A_IN
endmodule

module Dual_Ported_Register_File (
  input  CLK,
  input  WrEN,
  input  [3:0] WrREGNO,
  input  [3:0] RdREGNO1,
  input  [3:0] RdREGNO2,
  input  [31:0] INPUT,
  output [31:0] OUT1,
  output [31:0] OUT2
);

  wire En_a0, En_a1, En_a2, En_at, En_fp, En_k0, En_ra, En_s0, En_s1, En_s2, En_sp, En_t0, En_t1, En_t2,
       En_v0;
  wire [31:0] a0, a1, a2, at, fp, k0, ra, s0, s1, s2, sp, t0, t1, t2, v0, zero;

  Decoder #(.select(4), .disabled(0)) decoder_1 (
    .out1(En_at), .out2(En_v0), .out3(En_a0), .out4(En_a1), .out5(En_a2), .out6(En_t0), .out7(En_t1),
    .out8(En_t2), .out9(En_s0), .out10(En_s1), .out11(En_s2), .out12(En_k0), .out13(En_sp), .out14(En_fp),
    .out15(En_ra), .sel(WrREGNO), .en(WrEN));  // open: out0
  Register #(.width(32)) u_zero (.D(INPUT), .en(1'b0), .Q(zero), .clk(CLK));  // open: clr
  Register #(.width(32)) u_at (.D(INPUT), .en(En_at), .Q(at), .clk(CLK));  // open: clr
  Register #(.width(32)) u_v0 (.D(INPUT), .en(En_v0), .Q(v0), .clk(CLK));  // open: clr
  Register #(.width(32)) u_a0 (.D(INPUT), .en(En_a0), .Q(a0), .clk(CLK));  // open: clr
  Register #(.width(32)) u_a1 (.D(INPUT), .en(En_a1), .Q(a1), .clk(CLK));  // open: clr
  Register #(.width(32)) u_a2 (.D(INPUT), .en(En_a2), .Q(a2), .clk(CLK));  // open: clr
  Register #(.width(32)) u_t0 (.D(INPUT), .en(En_t0), .Q(t0), .clk(CLK));  // open: clr
  Register #(.width(32)) u_t1 (.D(INPUT), .en(En_t1), .Q(t1), .clk(CLK));  // open: clr
  Multiplexer #(.select(4), .width(32), .disabled(0), .enable("false")) multiplexer_1 (
    .in0(zero), .in1(at), .in2(v0), .in3(a0), .in4(a1), .in5(a2), .in6(t0), .in7(t1), .in8(t2), .in9(s0),
    .in10(s1), .in11(s2), .in12(k0), .in13(sp), .in14(fp), .in15(ra), .out(OUT2), .sel(RdREGNO2));
  Register #(.width(32)) u_t2 (.D(INPUT), .en(En_t2), .Q(t2), .clk(CLK));  // open: clr
  Register #(.width(32)) u_s0 (.D(INPUT), .en(En_s0), .Q(s0), .clk(CLK));  // open: clr
  Register #(.width(32)) u_s1 (.D(INPUT), .en(En_s1), .Q(s1), .clk(CLK));  // open: clr
  Register #(.width(32)) u_s2 (.D(INPUT), .en(En_s2), .Q(s2), .clk(CLK));  // open: clr
  Register #(.width(32)) u_k0 (.D(INPUT), .en(En_k0), .Q(k0), .clk(CLK));  // open: clr
  Register #(.width(32)) u_sp (.D(INPUT), .en(En_sp), .Q(sp), .clk(CLK));  // open: clr
  Register #(.width(32)) u_fp (.D(INPUT), .en(En_fp), .Q(fp), .clk(CLK));  // open: clr
  Register #(.width(32)) u_ra (.D(INPUT), .en(En_ra), .Q(ra), .clk(CLK));  // open: clr
  Multiplexer #(.select(4), .width(32), .disabled(0), .enable("false")) multiplexer_2 (
    .in0(zero), .in1(at), .in2(v0), .in3(a0), .in4(a1), .in5(a2), .in6(t0), .in7(t1), .in8(t2), .in9(s0),
    .in10(s1), .in11(s2), .in12(k0), .in13(sp), .in14(fp), .in15(ra), .out(OUT1), .sel(RdREGNO1));

  // Notes on the sheet:
  //   MODIFY AT YOUR OWN RISK
endmodule

module IF_IDRR_Buffer (
  input  in_1,
  input  in_2,
  input  [31:0] PC_N,
  input  [31:0] IR_IN,
  output [31:0] PC_OUT,
  output [3:0] OP_OUT,
  output [3:0] RX_OUT,
  output [3:0] RY_OUT,
  output [3:0] RZ_OUT,
  output [19:0] IMM_OUT
);

  Register #(.width(32)) PC (.D(PC_N), .Q(PC_OUT), .clk(in_1), .clr(in_2));  // open: en
  Register #(.width(32)) IR (.D(IR_IN), .Q({OP_OUT, RX_OUT, RY_OUT, IMM_OUT}), .clk(in_1), .clr(in_2));  // open: en

  assign RZ_OUT = IMM_OUT[3:0];

  // Other names for the same wires on the sheet: CLK = in_1; Flush = in_2
endmodule

module IDRR_EX_Buffer (
  input  CLK,
  input  SHF_A_IN,
  input  [3:0] OP_IN,
  input  [3:0] RX_IN,
  input  SHF_D_IN,
  input  [1:0] Func_IN,
  input  SW_IN,
  input  [31:0] IMM_IN,
  input  LW_IN,
  input  [31:0] Result_IN,
  input  [31:0] A_IN,
  input  [31:0] B_IN,
  output SHF_A_OUT,
  output [3:0] OP_OUT,
  output [3:0] RX_OUT,
  output SHF_D_OUT,
  output [1:0] Func_OUT,
  output SW_OUT,
  output [31:0] IMM_OUT,
  output LW_OUT,
  output [31:0] Result_OUT,
  output [31:0] A_OUT,
  output [31:0] B_OUT
);

  Register #(.width(1)) register_1 (.D(SHF_A_IN), .Q(SHF_A_OUT), .clk(CLK));  // open: en, clr
  Register #(.width(1)) register_2 (.D(SHF_D_IN), .Q(SHF_D_OUT), .clk(CLK));  // open: en, clr
  Register #(.width(1)) register_3 (.D(SW_IN), .Q(SW_OUT), .clk(CLK));  // open: en, clr
  Register #(.width(1)) register_4 (.D(LW_IN), .Q(LW_OUT), .clk(CLK));  // open: en, clr
  Register #(.width(4)) register_5 (.D(OP_IN), .Q(OP_OUT), .clk(CLK));  // open: en, clr
  Register #(.width(4)) register_6 (.D(RX_IN), .Q(RX_OUT), .clk(CLK));  // open: en, clr
  Register #(.width(2)) register_7 (.D(Func_IN), .Q(Func_OUT), .clk(CLK));  // open: en, clr
  Register #(.width(32)) register_8 (.D(IMM_IN), .Q(IMM_OUT), .clk(CLK));  // open: en, clr
  Register #(.width(32)) register_9 (.D(Result_IN), .Q(Result_OUT), .clk(CLK));  // open: en, clr
  Register #(.width(32)) register_10 (.D(A_IN), .Q(A_OUT), .clk(CLK));  // open: en, clr
  Register #(.width(32)) register_11 (.D(B_IN), .Q(B_OUT), .clk(CLK));  // open: en, clr
endmodule

module EX_MEM_Buffer (
  input  in_1,
  input  SW_IN,
  input  LW_IN,
  input  [3:0] RX_IN,
  input  [3:0] OP_IN,
  input  [31:0] B_IN,
  input  [31:0] RESULT_IN,
  output SW_OUT,
  output LW_OUT,
  output [3:0] RX_OUT,
  output [3:0] OP_OUT,
  output [31:0] B_OUT,
  output [31:0] RESULT_OUT
);

  Register #(.width(1)) register_1 (.D(SW_IN), .Q(SW_OUT), .clk(in_1));  // open: en, clr
  Register #(.width(1)) register_2 (.D(LW_IN), .Q(LW_OUT), .clk(in_1));  // open: en, clr
  Register #(.width(4)) register_3 (.D(RX_IN), .Q(RX_OUT), .clk(in_1));  // open: en, clr
  Register #(.width(4)) register_4 (.D(OP_IN), .Q(OP_OUT), .clk(in_1));  // open: en, clr
  Register #(.width(32)) register_5 (.D(B_IN), .Q(B_OUT), .clk(in_1));  // open: en, clr
  Register #(.width(32)) register_6 (.D(RESULT_IN), .Q(RESULT_OUT), .clk(in_1));  // open: en, clr

  // Other names for the same wires on the sheet: CLK = in_1
endmodule

module MEM_WB_Buffer (
  input  CLK,
  input  SW_IN,
  input  [3:0] RX_IN,
  input  [3:0] OP_IN,
  input  [31:0] RESULT_IN,
  output SW_OUT,
  output [3:0] RX_OUT,
  output [3:0] OP_OUT,
  output [31:0] RESULT_OUT
);

  Register #(.width(1)) register_1 (.D(SW_IN), .Q(SW_OUT), .clk(CLK));  // open: en, clr
  Register #(.width(4)) register_2 (.D(RX_IN), .Q(RX_OUT), .clk(CLK));  // open: en, clr
  Register #(.width(4)) register_3 (.D(OP_IN), .Q(OP_OUT), .clk(CLK));  // open: en, clr
  Register #(.width(32)) register_4 (.D(RESULT_IN), .Q(RESULT_OUT), .clk(CLK));  // open: en, clr
endmodule

module Regs (
  input  CK,
  input  WB,
  input  [3:0] OP_IN,
  input  [3:0] RX_IN,
  input  [3:0] RY_IN,
  input  [3:0] RZ_IN,
  input  [3:0] WB_RX,
  input  [31:0] RESULT_IN,
  output [31:0] A,
  output [31:0] B,
  output Use_IMM,
  output [1:0] Func,
  output BR,
  output BEQ,
  output JALR,
  output LDR,
  output STR,
  output Use_RZ
);

  wire [3:0] multiplexer_1_out;

  Multiplexer #(.width(4), .enable("false")) multiplexer_1 (
    .in0(RX_IN), .in1(RZ_IN), .out(multiplexer_1_out), .sel(Use_RZ));
  ROM #(.addrWidth(4), .dataWidth(9)) rom_1 (
    .addr(OP_IN), .data({Use_RZ, Use_IMM, Func, BR, BEQ, JALR, LDR, STR}));  // open: sel
  Dual_Ported_Register_File dual_ported_register_file_1 (
    .CLK(CK), .WrREGNO(WB_RX), .RdREGNO1(RY_IN), .RdREGNO2(multiplexer_1_out), .INPUT(RESULT_IN), .OUT1(A),
    .OUT2(B), .WrEN(WB));

  // Other names for the same wires on the sheet: SW = STR; LW = LDR; CLK = CK; OP[3:0] = OP_IN; RX[3:0] = RX_IN;
  //   RY[3:0] = RY_IN; RZ[3:0] = RZ_IN

  // Notes on the sheet:
  //   contents of rom_1 (hex, n*v repeats v):
  //   100 80 120 98 4 82 80 1 e0 90
endmodule

module ALU (
  input  [31:0] A,
  input  [31:0] B,
  input  A_2,
  input  D,
  input  [1:0] Func,
  output [31:0] Out
);

  wire [31:0] adder_1_out, adder_2_out, multiplexer_1_out, nand_1_out, shifter_1_out, shifter_2_out,
       shifter_3_out;

  Shifter #(.width(32)) shifter_1 (.in(A), .\dist (B[4:0]), .out(shifter_1_out));
  Shifter #(.width(32), .shift("lr")) shifter_2 (.in(A), .\dist (B[4:0]), .out(shifter_2_out));
  Shifter #(.width(32), .shift("ar")) shifter_3 (.in(A), .\dist (B[4:0]), .out(shifter_3_out));
  Adder #(.width(32)) adder_1 (.a(A), .b(B), .out(adder_1_out));  // open: cin, cout
  assign nand_1_out = ~(A & B);  // NAND_Gate nand_1, 32 bits wide
  Adder #(.width(32)) adder_2 (.a(A), .b(32'h1), .out(adder_2_out));  // open: cin, cout
  Multiplexer #(.select(2), .width(32), .disabled(0), .enable("false")) multiplexer_1 (
    .in0(shifter_1_out), .in1(shifter_2_out), .in2(shifter_1_out), .in3(shifter_3_out),
    .out(multiplexer_1_out), .sel({A_2, D}));
  Multiplexer #(.select(2), .width(32), .disabled(0), .enable("false")) multiplexer_2 (
    .in0(adder_1_out), .in1(nand_1_out), .in2(adder_2_out), .in3(multiplexer_1_out), .out(Out), .sel(Func));
endmodule

module IF (
  input  CLK,
  input  JALR,
  input  [31:0] PC___Off,
  input  [31:0] JALR_PC,
  input  BR,
  output [31:0] PC_OUT,
  output [31:0] IR_OUT
);

  wire [31:0] multiplexer_1_out, PC_q;

  Adder #(.width(32)) adder_1 (.a(PC_q), .b(32'h1), .out(PC_OUT));  // open: cin, cout
  // Probe on PC___Off
  Register #(.width(32)) PC (.D(multiplexer_1_out), .Q(PC_q), .clk(CLK));  // open: en, clr
  Multiplexer #(.select(2), .width(32), .enable("false")) multiplexer_1 (
    .in0(PC_OUT), .in1(PC___Off), .in2(JALR_PC), .in3(JALR_PC), .out(multiplexer_1_out), .sel({JALR, BR}));
  RAM #(.addrWidth(24), .dataWidth(32)) ram_1 (.addr(PC_q[23:0]), .data(IR_OUT), .clk(CLK));  // open: sel, ld, clr
endmodule

module ID (
  input  CLK,
  input  [19:0] IMM_IN,
  input  WB,
  input  [31:0] PC_IN,
  input  [3:0] OP_IN,
  input  [3:0] RX_IN,
  input  [3:0] RY_IN,
  input  [31:0] WB_RESULT,
  input  [3:0] RZ_IN,
  input  [3:0] WB_RX,
  input  [31:0] NEW_A,
  input  [31:0] NEW_B,
  output I_Type,
  output SW,
  output SHF_A,
  output LW,
  output SHF_D,
  output BR_Cond,
  output JALR,
  output [1:0] Func,
  output [3:0] OP_OUT,
  output Use_RZ,
  output [3:0] RX_OUT,
  output [31:0] IMM_OUT,
  output [31:0] RESULT,
  output [31:0] A_OUT,
  output [31:0] B_OUT
);

  wire BEQ, BR, comparator_1_eq, xnor_1_out;

  assign IMM_OUT = {{12{IMM_IN[19]}}, IMM_IN};  // Bit_Extender bit_extender_1
  Regs regs_1 (
    .OP_IN(OP_IN), .RX_IN(RX_IN), .RY_IN(RY_IN), .RZ_IN(RZ_IN), .CK(CLK), .A(A_OUT), .B(B_OUT),
    .Use_IMM(I_Type), .Func(Func), .BEQ(BEQ), .JALR(JALR), .LDR(LW), .STR(SW), .BR(BR), .WB(WB),
    .RESULT_IN(WB_RESULT), .WB_RX(WB_RX), .Use_RZ(Use_RZ));
  Adder #(.width(32)) adder_1 (.a(IMM_OUT), .b(PC_IN), .out(RESULT));  // open: cin, cout
  Comparator #(.width(32)) comparator_1 (.a(NEW_A), .b(NEW_B), .eq(comparator_1_eq));  // open: gt, lt
  // Probe on A_OUT
  // Probe on B_OUT
  and and_1 (BR_Cond, BR, xnor_1_out);
  xnor xnor_1 (xnor_1_out, comparator_1_eq, BEQ);

  assign OP_OUT = OP_IN;
  assign RX_OUT = RX_IN;
  assign SHF_A = IMM_IN[19];
  assign SHF_D = IMM_IN[18];
endmodule

module EX (
  input  [1:0] Func,
  input  I_Type,
  input  [31:0] A_IN,
  input  [31:0] B_IN,
  input  [31:0] IMM_IN,
  input  SHF_A,
  input  SHF_D,
  input  SW_IN,
  input  LW_IN,
  input  [3:0] OP_IN,
  input  [3:0] RX_IN,
  output SW_OUT,
  output LW_OUT,
  output [3:0] OP_OUT,
  output [3:0] RX_OUT,
  output [31:0] B_OUT,
  output [31:0] RESULT
);

  Multiplexer #(.width(32), .enable("false")) multiplexer_1 (.in0(B_IN), .in1(IMM_IN), .out(B_OUT), .sel(I_Type));
  ALU alu_1 (.A(A_IN), .B(B_OUT), .Out(RESULT), .A_2(SHF_A), .D(SHF_D), .Func(Func));

  assign LW_OUT = LW_IN;
  assign OP_OUT = OP_IN;
  assign RX_OUT = RX_IN;
  assign SW_OUT = SW_IN;
endmodule

module MEM (
  input  CLK,
  input  SW_IN,
  input  LW_IN,
  input  [3:0] RX_IN,
  input  [3:0] OP_IN,
  input  [31:0] B_IN,
  input  [31:0] RESULT_IN,
  output SW_OUT,
  output [3:0] RX_OUT,
  output [3:0] OP_OUT,
  output [31:0] RESULT_OUT
);

  wire [31:0] ram_1_data;

  RAM #(.addrWidth(24), .dataWidth(32), .bus("separate")) ram_1 (
    .addr(RESULT_IN[23:0]), .din(B_IN), .data(ram_1_data), .str(SW_IN));  // open: sel, clk, ld, clr
  Multiplexer #(.width(32), .enable("false")) multiplexer_1 (
    .in0(RESULT_IN), .in1(ram_1_data), .out(RESULT_OUT), .sel(LW_IN));

  assign OP_OUT = OP_IN;
  assign RX_OUT = RX_IN;
  assign SW_OUT = SW_IN;
endmodule

module WB (
  input  SW_IN,
  input  [3:0] RX_IN,
  input  [3:0] OP_IN,
  input  [31:0] RESULT_IN,
  output out_5,
  output [3:0] RX_OUT,
  output [31:0] RESULT_OUT
);

  wire and_1_out, not_1_out, not_2_out, xor_1_out;

  not not_1 (not_1_out, OP_IN[0]);
  and and_1 (and_1_out, not_1_out, not_2_out);
  not not_2 (not_2_out, OP_IN[1]);
  xor xor_1 (xor_1_out, OP_IN[1], OP_IN[0]);
  or or_1 (out_5, and_1_out, xor_1_out);

  assign RESULT_OUT = RESULT_IN;
  assign RX_OUT = RX_IN;

  // Other names for the same wires on the sheet: WB_OUT = out_5
endmodule

module Forwarder (
  input  [3:0] E_RX,
  input  [3:0] M_RX,
  input  [31:0] A,
  input  [31:0] E_Result,
  input  [31:0] M_Result,
  input  [31:0] B,
  input  [3:0] RX,
  input  [3:0] RY,
  input  [3:0] RZ,
  input  Use_RZ,
  output [31:0] A_OUT,
  output [31:0] B_OUT
);

  wire [1:0] comparator_1_eq, comparator_3_eq;
  wire [3:0] multiplexer_1_out;

  Multiplexer #(.width(4), .enable("false")) multiplexer_1 (.in0(RX), .in1(RZ), .out(multiplexer_1_out), .sel(Use_RZ));
  Comparator #(.width(4)) comparator_1 (.a(E_RX), .b(multiplexer_1_out), .eq(comparator_1_eq[0]));  // open: gt, lt
  Comparator #(.width(4)) comparator_2 (.a(multiplexer_1_out), .b(M_RX), .eq(comparator_1_eq[1]));  // open: gt, lt
  Comparator #(.width(4)) comparator_3 (.a(E_RX), .b(RY), .eq(comparator_3_eq[0]));  // open: gt, lt
  Comparator #(.width(4)) comparator_4 (.a(RY), .b(M_RX), .eq(comparator_3_eq[1]));  // open: gt, lt
  Multiplexer #(.select(2), .width(32), .enable("false")) multiplexer_2 (
    .in0(B), .in1(E_Result), .in2(M_Result), .in3(E_Result), .out(B_OUT), .sel(comparator_1_eq));
  Multiplexer #(.select(2), .width(32), .enable("false")) multiplexer_3 (
    .in0(A), .in1(E_Result), .in2(M_Result), .in3(E_Result), .out(A_OUT), .sel(comparator_3_eq));
endmodule
